# Fritzing sketch foodbot_foodbot_dircuit _diagram (saved by Fritzing 0.9.3b)

parts:
  Mod1 = generic-ac-power-supply [package=THT]
  U1 = ESP8266 WiFi Module [part_number=ESP8266]
  J1 = Basic Servo
  J2 = Basic Servo
  J4 = Basic Servo
  J5 = Basic Servo
  J6 = Basic Servo
  J8 = Basic Servo
  HC-SR04_Sensor_1 = HC-SR04 Ultrasonic Distance Sensor
  HC-SR04_Sensor_2 = HC-SR04 Ultrasonic Distance Sensor
  HC-SR04_Sensor_3 = HC-SR04 Ultrasonic Distance Sensor
  HC-SR04_Sensor_4 = HC-SR04 Ultrasonic Distance Sensor
  HC-SR04_Sensor_5 = HC-SR04 Ultrasonic Distance Sensor
  HC-SR04_Sensor_6 = HC-SR04 Ultrasonic Distance Sensor
  HC-SR04_Sensor_7 = HC-SR04 Ultrasonic Distance Sensor
  HC-SR04_Sensor_8 = HC-SR04 Ultrasonic Distance Sensor
  Part1 = Arduino Mega ADK (Rev3)
  Power_plug1 = Power plug
  J9 = Basic Servo
  J10 = Basic Servo
  L298N1 = L298N DC motor driver
  M2 = Stepper Motor - Bipolar

nets:
  N1: Mod1.pin1, Power_plug1.VCC
  N2: Mod1.pin2, Power_plug1.GND
  N3: Mod1.pin3#2, L298N1.12V
  GND: Mod1.pin3#3, U1.GND, Part1.GND, L298N1.GND
  N4: U1.RXD, Part1.D18/TX1
  N5: U1.VCC, U1.CH_PD
  N6: U1.TXD, Part1.D19/RX1
  GND_2: J1.gnd, J2.gnd, J4.gnd, J5.gnd, J6.gnd, J8.gnd, J10.gnd
  VCC: J1.vcc, J2.vcc, J4.vcc, J5.vcc, J8.vcc, J9.vcc, J10.vcc
  N7: J1.pulse, Part1.D1/TX0
  N8: J2.pulse, Part1.D2_PWM
  N9: J4.pulse, Part1.D4_PWM
  N10: J5.pulse, Part1.D5_PWM
  N11: J6.pulse, Part1.D7_PWM
  N12: J8.pulse, Part1.D6_PWM
  VCC_2: HC-SR04_Sensor_1.VCC, HC-SR04_Sensor_6.VCC
  N13: HC-SR04_Sensor_1.TRIG, HC-SR04_Sensor_6.TRIG
  N14: HC-SR04_Sensor_1.ECHO, Part1.D13_PWM
  GND_3: HC-SR04_Sensor_1.GND, HC-SR04_Sensor_6.GND
  N15: HC-SR04_Sensor_2.ECHO, Part1.D12_PWM
  N16: HC-SR04_Sensor_3.ECHO, Part1.D14/TX3
  N17: HC-SR04_Sensor_4.ECHO, Part1.D11_PWM
  N18: HC-SR04_Sensor_5.ECHO, Part1.D15/RX3
  N19: HC-SR04_Sensor_6.ECHO, Part1.D20/SDA
  N20: HC-SR04_Sensor_7.ECHO, Part1.D16/TX2
  N21: HC-SR04_Sensor_8.ECHO, Part1.D17/RX2
  N22: Part1.D8_PWM, J10.pulse
  N23: Part1.5V, L298N1.5V#7
  N24: Part1.D3_PWM, J9.pulse
  N25: Part1.D44, L298N1.IN2
  N26: Part1.D45, L298N1.IN1
  N27: Part1.D46, L298N1.IN4
  N28: Part1.D47, L298N1.IN3
  N29: L298N1.OUT1, M2.C
  N30: L298N1.OUT2, M2.A
  N31: L298N1.OUT3, M2.B
  N32: L298N1.OUT4, M2.D
  N33: L298N1.5V#9, L298N1.5V#10

custom parts:
  generic-ac-power-supply: Generic ac power supply module. Use as is, or customize the svgs to fit your particular device (as they are all different.) Provides AC input and single DC output. PCB is generic and will need modifications if you intend to do a pcb mount.
  ESP8266 WiFi Module: Generic WiFi Module based on the ESP8266 with onboard PCB antenna and UART communications
  L298N DC motor driver: 2x DC motor driver with 78M05 positive voltage regulator (7..35 V) L298N: max 46 V, 2 A Set 5 V Enable jumper to enable 5 V regultor (needed for the L298N) and +5 V output at screw terminal or supply external +5 V at screw terminal Set ENA and/or ENB to +5 V to enable motor permanently or supply ENA and/or ENB with PWM signal IN1 and IN2 set rotation directory for motor A (OUT1/OUT2) IN2 and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
